# Fritzing sketch ButtsDpad (saved by Fritzing 0.9.10b)
circuit board: 2.81707cm x 2.80239cm

parts:
  S1 = Momentary Switch 6mm 2pin
  S2 = Momentary Switch 6mm 2pin
  S3 = Momentary Switch 6mm 2pin
  J1 = female pin header, 5 pins [form="♀ (female)"]
  S4 = Momentary Switch 6mm 2pin

nets:
  N1: S1.1, J1.pin2
  N2: S1.2, S2.2, S3.2, J1.pin5, S4.2
  N3: S2.1, J1.pin1
  N4: S3.1, J1.pin4
  N5: J1.pin3, S4.1

custom parts:
  Momentary Switch 6mm 2pin: Momentary Switch 6mm 2 pin Button commonly used for reset or general input.
