# Fritzing sketch ButtsFront (saved by Fritzing 0.9.10b)
circuit board: 3.30763cm x 1.30839cm

parts:
  S1 = SWITCH-MOMENTARY-2 [package=tactile-pth-12mm]
  S2 = SWITCH-MOMENTARY-2 [package=tactile-pth-12mm]
  JP1 = Header 3 [package=jst-3-pth]

nets:
  N1: S1.1, JP1.2
  N2: S1.2, S2.1, JP1.3
  N3: S2.2, JP1.1
