# Fritzing sketch Gamepad V1 (saved by Fritzing 0.9.10b)

parts:
  Part1 = Arduino Pro Micro (Clone)
  S5 = Pushbutton [package="[THT]"]
  S6 = Pushbutton [package="[THT]"]
  S7 = Pushbutton [package="[THT]"]
  S8 = Pushbutton [package="[THT]"]
  R5 = Resistor [tolerance=±5% power=0.25 resistance=10k package=THT]
  R6 = Resistor [tolerance=±5% power=0.25 resistance=10k package=THT]
  R7 = Resistor [tolerance=±5% power=0.25 resistance=10k package=THT]
  R8 = Resistor [tolerance=±5% power=0.25 resistance=10k package=THT]
  S15 = Pushbutton [package="[THT]"]
  S16 = Pushbutton [package="[THT]"]
  S17 = Pushbutton [package="[THT]"]
  S18 = Pushbutton [package="[THT]"]
  R9 = Resistor [tolerance=±5% power=0.25 resistance=10k package=THT]
  R10 = Resistor [tolerance=±5% power=0.25 resistance=10k package=THT]
  R11 = Resistor [tolerance=±5% power=0.25 resistance=10k package=THT]
  R12 = Resistor [tolerance=±5% power=0.25 resistance=10k package=THT]
  Part2 = Thumb Joystick  # not connected
  Part3 = Thumb Joystick  # not connected
  S19 = Pushbutton [package="[THT]"]  # not connected
  S20 = Pushbutton [package="[THT]"]  # not connected
  S21 = Pushbutton [package="[THT]"]  # not connected
  S22 = Pushbutton [package="[THT]"]  # not connected
  S23 = Pushbutton [package="[THT]"]  # not connected
  S24 = Pushbutton [package="[THT]"]  # not connected
  U1 = 74HC165 [part_number=SN74LS165 package="DIP16 [THT]"]

nets:
  GND: Part1.GND, R12.Pin_0, U1.GND
  N1: Part1.D9, S15.Pin_3, S15.Pin_4, R11.Pin_1
  N2: Part1.D10, U1.Q2
  N3: Part1.D16, U1.Q7'
  N4: Part1.D14, U1.Q0
  N5: Part1.D15, U1.Q1
  VCC: Part1.VCC, U1.VCC
  N6: S5.Pin_1, S5.Pin_2, S6.Pin_2, S7.Pin_3, S7.Pin_4, S8.Pin_3
  N7: S5.Pin_3, S5.Pin_4, R7.Pin_1
  N8: S6.Pin_3, S6.Pin_4, R6.Pin_1
  N9: S7.Pin_1, S7.Pin_2, R5.Pin_1
  N10: S8.Pin_1, S8.Pin_2, R8.Pin_1
  N11: S15.Pin_1, S15.Pin_2, S16.Pin_2, S17.Pin_3, S17.Pin_4, S18.Pin_3
  N12: S16.Pin_3, S16.Pin_4, R10.Pin_1
  N13: S17.Pin_1, S17.Pin_2, R9.Pin_1
  N14: S18.Pin_1, S18.Pin_2, R12.Pin_1

custom parts:
  74HC165: 8-bit parallel-load shift registers
