# Fritzing sketch Gamepad V2 (saved by Fritzing 0.9.10b)
circuit board: 5.83049cm x 3.79657cm

parts:
  Part1 = Arduino Pro Micro (Clone)
  U3 = 74HC4052 [package=so16]
  J1 = female pin header, 5 pins [form="♀ (female)"]
  J3 = female pin header, 5 pins [form="♀ (female)"]
  J5 = female pin header, 3 pins [form="♀ (female)"]
  J6 = female pin header, 3 pins [form="♀ (female)"]
  S1 = Momentary Switch 6mm 2pin
  S2 = Momentary Switch 6mm 2pin
  J4 = female pin header, 5 pins [form="♀ (female)"]
  J2 = female pin header, 5 pins [form="♀ (female)"]
  R1 = Resistor [tolerance=±5% resistance=10k power=0.25 package=THT]
  R2 = Resistor [tolerance=±5% resistance=10k power=0.25 package=THT]
  R4 = Resistor [tolerance=±5% resistance=10k power=0.25 package=THT]
  R8 = Resistor [tolerance=±5% resistance=10k power=0.25 package=THT]
  R6 = Resistor [tolerance=±5% resistance=10k power=0.25 package=THT]
  R9 = Resistor [tolerance=±5% resistance=10k power=0.25 package=THT]
  R10 = Resistor [tolerance=±5% resistance=10k power=0.25 package=THT]
  R11 = Resistor [tolerance=±5% resistance=10k power=0.25 package=THT]

nets:
  GND: Part1.GND, U3.GND, J3.pin1, J5.pin1, J6.pin1, S1.1, S2.1, J4.pin1, R1.Pin_0, R2.Pin_0, R4.Pin_0, R8.Pin_1, R6.Pin_1, R9.Pin_1, R10.Pin_1, R11.Pin_0
  N1: Part1.D2, U3.B
  N2: Part1.D3, S2.2
  N3: Part1.D4, J6.pin2
  N4: Part1.D5, J6.pin3
  N5: Part1.D6, U3.X2
  N6: Part1.D7, J3.pin3
  N7: Part1.D8, J3.pin5
  N8: Part1.D9, J3.pin4
  N9: Part1.D10, U3.Y2
  N10: Part1.D16, U3.Y0
  N11: Part1.D14, J5.pin3
  N12: Part1.D15, J5.pin2
  N13: Part1.A0, S1.2
  N14: Part1.A1, J4.pin5
  N15: Part1.A2, J4.pin4
  N16: Part1.A3, J4.pin3
  VCC: Part1.VCC, U3.VCC, J1.pin1, J3.pin2, J4.pin2, J2.pin1
  N17: U3.Y, J2.pin3, R2.Pin_1
  N18: U3.Y3, J2.pin2, R1.Pin_1
  N19: U3.Y1, J2.pin5, R4.Pin_1
  N20: U3.INH, J2.pin4, R11.Pin_1
  N21: U3.X3, J1.pin2, R10.Pin_0
  N22: U3.X0, J1.pin3, R6.Pin_0
  N23: U3.X, J1.pin4, R8.Pin_0
  N24: U3.X1, J1.pin5, R9.Pin_0

custom parts:
  Momentary Switch 6mm 2pin: Momentary Switch 6mm 2 pin Button commonly used for reset or general input.
